# Fritzing sketch watering-system_schema (saved by Fritzing 0.9.3b)

parts:
  WeMos_D1_Mini1 = WeMos D1 Mini
  hc-sr1 = hc-sr04
  Součástka2 = IFR520 MOS module [package=THT]
  Součástka3 = FC-28 Soil Hygrometer Module
  MUX1 = 74HC4051 [package="DIP (Dual Inline) [THT]"]
  Součástka4 = IFR520 MOS module [package=THT]
  Součástka5 = FC-28 Soil Hygrometer Module
  Součástka6 = FC-28 Soil Hygrometer Module
  Součástka7 = FC-28 Soil Hygrometer Module
  M1 = DC Motor
  M2 = DC Motor
  Součástka8 = FC-28 Soil Hygrometer Module
  Součástka9 = GY-BMEP280 Barometric Pressure Sensor - Breakout
  Q1 = Basic FET N-Channel [package="D2Pak [SMD]"]

nets:
  VCC: WeMos_D1_Mini1.3V3, Součástka2.VCC, Součástka3.VCC, MUX1.VDD, Součástka4.VCC, Součástka5.VCC, Součástka6.VCC, Součástka7.VCC, Součástka8.VCC, Součástka9.VCC, Součástka9.CSB, Součástka9.SDO
  5V: WeMos_D1_Mini1.5V, hc-sr1.VCC
  N1: WeMos_D1_Mini1.A0, MUX1.IO
  N2: WeMos_D1_Mini1.D0, MUX1.A
  N3: WeMos_D1_Mini1.D1, Součástka9.SCL
  N4: WeMos_D1_Mini1.D2, Součástka9.SDA
  N5: WeMos_D1_Mini1.D3, hc-sr1.Echo
  N6: WeMos_D1_Mini1.D4, hc-sr1.Trig
  N7: WeMos_D1_Mini1.D5, MUX1.B
  N8: WeMos_D1_Mini1.D6, MUX1.C
  N9: WeMos_D1_Mini1.D7, Součástka2.SIG
  N10: WeMos_D1_Mini1.D8, Součástka4.SIG
  GND: WeMos_D1_Mini1.G, hc-sr1.GND, MUX1.VEE, MUX1.VSS, Součástka4.GND, Q1.source
  N11: WeMos_D1_Mini1.RX, Q1.Gate
  GND_2: Součástka2.GND, MUX1.INH, Součástka9.GND
  N12: Součástka2.V+, M1.pin_1
  N13: Součástka2.V-, M1.pin_2
  GND_3: Součástka3.GND, Součástka5.GND, Součástka6.GND, Součástka7.GND, Součástka8.GND, Q1.drain
  N14: Součástka3.AO, MUX1.IO2
  N15: MUX1.IO4, Součástka8.AO
  N16: MUX1.IO3, Součástka5.AO
  N17: MUX1.IO0, Součástka6.AO
  N18: MUX1.IO1, Součástka7.AO
  N19: Součástka4.V+, M2.pin_1
  N20: Součástka4.V-, M2.pin_2

notes:
  GY-BME280-3.3

custom parts:
  FC-28 Soil Hygrometer Module: The FC-28 is a soil hygrometer module that uses the Texas Instruments LM393 comparator chip to provide an analog measurement of soil humidity. The digital output is high when soil moisture is over a certain threshold, as determined by adjusting the potentiometer.
  74HC4051: 8 channel analog multiplexer/demultiplexer
  GY-BMEP280 Barometric Pressure Sensor - Breakout: The BME280 is a chip which was originally designed for the next generation of smartphones. It is made up of a very accurate pressure sensor and an associated temperature sensor which helps calibrate the pressure readings. And just for fun they threw in a pretty solid humidity sensor in there as well! So with an I2C connection you have access to enough weather data to make some pretty good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
